# Fritzing sketch raspi_lcdinfo (saved by Fritzing 0.7.10b)
breadboards: 1

parts:
  RaspberryPi1 = Raspberry Pi Model B
  LCD1 = LCD screen
  DS1 = DS18B20 1-Wire Temperature Sensor [part_number=DS18B20]
  R1 = Resistor [tolerance=±1% resistance=4.7k package=THT]
  R2 = Basic Potentiometer [package=THT]

nets:
  VDD: RaspberryPi1.5V, LCD1.VDD, DS1.VDD, R1.Pin_0, R2.leg1
  N1: RaspberryPi1.SDA, RaspberryPi1.SCL, LCD1.LED+
  GND: RaspberryPi1.GND, RaspberryPi1.TXD, LCD1.VSS, LCD1.LED-, DS1.GND, R2.leg2
  N2: RaspberryPi1.#4, DS1.DQ, R1.Pin_1
  N3: RaspberryPi1.#17, LCD1.E
  N4: RaspberryPi1.#18, LCD1.RS
  N5: RaspberryPi1.#21, LCD1.DB4
  N6: RaspberryPi1.#22, LCD1.DB5
  N7: RaspberryPi1.#23, LCD1.DB6
  N8: RaspberryPi1.#24, LCD1.DB7
  N9: LCD1.V0, R2.wiper

custom parts:
  Raspberry Pi Model B: Raspberry Pi (Model B)
